# Fritzing sketch Flood  Sketch (saved by Fritzing 0.8.7b)
breadboards: 1

parts:
  Water_Level_Sensor1 = Water Level Sensor
  Part1 = Arduino Nano (Rev3.0)
  Part2 = Bluetooth HM-10

nets:
  N1: Water_Level_Sensor1.SIG, Part1.A5
  VCC: Water_Level_Sensor1.VCC, Part1.5V, Part2.VCC
  GND: Water_Level_Sensor1.GND, Part1.GND, Part2.GND
  N2: Part1.D1/TX, Part2.RXD
  N3: Part1.D0/RX, Part2.TXD

custom parts:
  Water Level Sensor: A water level sensor. This sensor operates at 3V to 5V. The Sig (signal) pin outputs an analogue signal that is in proportion to the amount of water in contact with the sensor.
